# Fritzing sketch wiring_diagram (saved by Fritzing 0.9.3b)

parts:
  Part1 = SparkFun Qwiic SHIM for Raspberry Pi [part_number="SparkFun #15794"]
  Part2 = Adafruit BMP388 [part_number="Adafruit #3966"]
  Raspberry_Pi1 = Raspberry Pi Zero  # not connected
  AM1 = AM2320 Humidity and Temperature Sensor

nets:
  GND: Part1.GND, Part2.GND, AM1.GND
  VCC: Part1.VCC, Part2.VCC
  N1: Part1.SDA, Part2.SDI/SDA, AM1.SDA
  N2: Part1.SCL, Part2.SCK/SCL, AM1.SCL
  3.3V: Part2.3.3V, AM1.VDD

custom parts:
  SparkFun Qwiic SHIM for Raspberry Pi: The SparkFun Qwiic SHIM for Raspberry Pi is a small, easily removable breakout that easily adds a Qwiic connector to your Raspberry Pi. The SHIM design allows you to plug directly to the Pi's I2C bus with no soldering required and the thin PCB design allows for it to be sandwiched on your Pi GPIO with other HATs! The Qwiic SHIM works great when you do not need the full capabilities of the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
  Adafruit BMP388: Bosch has been a leader in barometric pressure sensors, from the BMP085. BMP180, and BMP280... now we've got the next generation, the Adafruit BMP388 Precision Barometric Pressure sensor. As you would expect, this sensor is similar to its earlier versions but even better. The BMP388 has better precision than ever, which makes it excellent for environmental sensing or as a precision altimeter.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
  Raspberry Pi Zero: The Raspberry Pi Zero is the latest single board computer to be released by the Raspberry Pi Foundation. It is the entry level model Raspberry Pi perfect for hobbyists, makers and industrial engineers looking to create solutions where small size and low power consumption are important. This is especially relevant for applications in the wearables space as well as up and coming applications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
